// Logisim project Shift Right AND Left Registers.circ as structural Verilog: 1 circuit, main circuit main
module main (
  input  In,
  input  IN_2,
  input  Reset,
  output out_4,
  output out_5,
  output out_6,
  output out_7,
  output out_8
);

  wire clock_1_out, clock_2_out, d_ff_6_q, d_ff_8_q;

  Clock clock_1 (.out(clock_1_out));
  D_Flip_Flop d_ff_1 (.clk(clock_2_out), .D(Reset), .Q(out_8), .reset(Reset));  // open: Qn, preset, en
  Clock clock_2 (.out(clock_2_out));
  D_Flip_Flop d_ff_2 (.clk(clock_1_out), .D(In), .Q(out_4));  // open: Qn, preset, en, reset
  D_Flip_Flop d_ff_3 (.clk(clock_1_out), .D(out_4), .Q(out_5));  // open: Qn, preset, en, reset
  D_Flip_Flop d_ff_4 (
    .clk(clock_2_out), .D(d_ff_6_q), .Q(Reset), .preset(Reset), .en(Reset), .reset(Reset));  // open: Qn
  D_Flip_Flop d_ff_5 (.clk(clock_1_out), .D(out_5), .Q(out_6));  // open: Qn, preset, en, reset
  D_Flip_Flop d_ff_6 (.clk(clock_2_out), .D(d_ff_8_q), .Q(d_ff_6_q), .reset(Reset));  // open: Qn, preset, en
  D_Flip_Flop d_ff_7 (.clk(clock_1_out), .D(out_6), .Q(out_7));  // open: Qn, preset, en, reset
  D_Flip_Flop d_ff_8 (.clk(clock_2_out), .D(IN_2), .Q(d_ff_8_q), .reset(Reset));  // open: Qn, preset, en

  // Notes on the sheet:
  //   Shift right register
  //   Shift Left Register
endmodule
