// Logisim project d flip-flip.circ as structural Verilog: 1 circuit, main circuit main
module main (
  input  D,
  input  C
);

  wire nand_1_out, nand_2_out, nand_3_out, nand_4_out, not_1_out;

  Clock clock_1 (.out(C));
  not not_1 (not_1_out, D);
  nand nand_1 (nand_1_out, D, C);
  nand nand_2 (nand_2_out, not_1_out, C);
  nand nand_3 (nand_3_out, nand_1_out, nand_4_out);
  nand nand_4 (nand_4_out, nand_3_out, nand_2_out);
  LED led_1 (.in(nand_3_out));
  LED led_2 (.in(nand_4_out));

  // Notes on the sheet:
  //   Q
endmodule
