// Logisim project sr-flip flop.circ as structural Verilog: 1 circuit, main circuit main
module main (
  input  S,
  input  R
);

  wire nand_1_out, nand_2_out;

  nand nand_1 (nand_1_out, S, nand_2_out);
  nand nand_2 (nand_2_out, nand_1_out, R);
  LED led_1 (.in(nand_1_out));
  LED led_2 (.in(nand_2_out));

  // Notes on the sheet:
  //   Q
  //   Q(o)
endmodule
